// Digital circuit 4_4pinesIO.dig as structural Verilog
module _4_4pinesIO (
  input  Set,
  input  Enable,
  input  Clear,
  input  Set_2,
  input  D7,
  input  Enable_2,
  input  Clear_2,
  input  D6,
  input  D5,
  input  D4,
  input  Clock,
  input  Set_3,
  input  Enable_3,
  input  Clear_3,
  input  D10,
  input  D9,
  input  D8,
  input  in_30,
  input  Input1,
  input  Input2,
  input  Input3,
  input  Input4,
  output out_4,
  output out_5,
  output out_6,
  output out_7,
  output out_15,
  output out_16,
  output out_17,
  output out_18,
  output out_26,
  output out_27,
  output out_28,
  output out_29,
  output Output1,
  output Output2,
  output Output3,
  output Output4
);

  wire driver_3_out, driver_5_out, driver_7_out, multiplexer_1_out, multiplexer_2_out, multiplexer_3_out,
       multiplexer_4_out, multiplexer_5_out, multiplexer_6_out, multiplexer_7_out, multiplexer_8_out,
       multiplexer_9_out, multiplexer_10_out, multiplexer_11_out, multiplexer_12_out, not_1_out, not_2_out,
       not_3_out, not_4_out, pulldown_1_out;

  Multiplexer multiplexer_1 (.sel(Enable_3), .in_0(out_26), .in_1(in_30), .out(multiplexer_1_out));
  D_FF_AS d_ff_as_1 (.Set(Set_3), .D(multiplexer_1_out), .C(Clock), .Clr(Clear_3), .Q(out_26));  // open: nQ
  not not_1 (not_1_out, out_26);
  Multiplexer multiplexer_2 (.sel(Enable_3), .in_0(out_27), .in_1(D10), .out(multiplexer_2_out));
  D_FF_AS d_ff_as_2 (.Set(Set_3), .D(multiplexer_2_out), .C(Clock), .Clr(Clear_3), .Q(out_27));  // open: nQ
  Multiplexer multiplexer_3 (.sel(Enable_3), .in_0(out_28), .in_1(D9), .out(multiplexer_3_out));
  not not_2 (not_2_out, out_27);
  D_FF_AS d_ff_as_3 (.Set(Set_3), .D(multiplexer_3_out), .C(Clock), .Clr(Clear_3), .Q(out_28));  // open: nQ
  not not_3 (not_3_out, out_28);
  Multiplexer multiplexer_4 (.sel(Enable_3), .in_0(out_29), .in_1(D8), .out(multiplexer_4_out));
  D_FF_AS d_ff_as_4 (.Set(Set_3), .D(multiplexer_4_out), .C(Clock), .Clr(Clear_3), .Q(out_29));  // open: nQ
  not not_4 (not_4_out, out_29);
  Multiplexer multiplexer_5 (.sel(Enable_2), .in_0(out_15), .in_1(D7), .out(multiplexer_5_out));
  PullDown pulldown_1 (.out(pulldown_1_out));
  D_FF_AS d_ff_as_5 (.Set(Set_2), .D(multiplexer_5_out), .C(Clock), .Clr(Clear_2), .Q(out_15));  // open: nQ
  assign pulldown_1_out = not_1_out ? Input4 : 1'bz;  // Driver driver_1
  Multiplexer multiplexer_6 (.sel(Enable), .in_0(out_4), .in_1(pulldown_1_out), .out(multiplexer_6_out));
  assign Output4 = out_26 ? out_15 : 1'bz;  // Driver driver_2
  Multiplexer multiplexer_7 (.sel(Enable_2), .in_0(out_16), .in_1(D6), .out(multiplexer_7_out));
  D_FF_AS d_ff_as_6 (.Set(Set), .D(multiplexer_6_out), .C(Clock), .Clr(Clear), .Q(out_4));  // open: nQ
  assign driver_3_out = not_2_out ? Input3 : 1'bz;  // Driver driver_3
  D_FF_AS d_ff_as_7 (.Set(Set_2), .D(multiplexer_7_out), .C(Clock), .Clr(Clear_2), .Q(out_16));  // open: nQ
  Multiplexer multiplexer_8 (.sel(Enable), .in_0(out_5), .in_1(driver_3_out), .out(multiplexer_8_out));
  assign Output3 = out_27 ? out_16 : 1'bz;  // Driver driver_4
  D_FF_AS d_ff_as_8 (.Set(Set), .D(multiplexer_8_out), .C(Clock), .Clr(Clear), .Q(out_5));  // open: nQ
  Multiplexer multiplexer_9 (.sel(Enable_2), .in_0(out_17), .in_1(D5), .out(multiplexer_9_out));
  D_FF_AS d_ff_as_9 (.Set(Set_2), .D(multiplexer_9_out), .C(Clock), .Clr(Clear_2), .Q(out_17));  // open: nQ
  assign driver_5_out = not_3_out ? Input2 : 1'bz;  // Driver driver_5
  Multiplexer multiplexer_10 (.sel(Enable), .in_0(out_6), .in_1(driver_5_out), .out(multiplexer_10_out));
  assign Output2 = out_28 ? out_17 : 1'bz;  // Driver driver_6
  Multiplexer multiplexer_11 (.sel(Enable_2), .in_0(out_18), .in_1(D4), .out(multiplexer_11_out));
  D_FF_AS d_ff_as_10 (.Set(Set), .D(multiplexer_10_out), .C(Clock), .Clr(Clear), .Q(out_6));  // open: nQ
  assign driver_7_out = not_4_out ? Input1 : 1'bz;  // Driver driver_7
  D_FF_AS d_ff_as_11 (.Set(Set_2), .D(multiplexer_11_out), .C(Clock), .Clr(Clear_2), .Q(out_18));  // open: nQ
  Multiplexer multiplexer_12 (.sel(Enable), .in_0(out_7), .in_1(driver_7_out), .out(multiplexer_12_out));
  assign Output1 = out_29 ? out_18 : 1'bz;  // Driver driver_8
  D_FF_AS d_ff_as_12 (.Set(Set), .D(multiplexer_12_out), .C(Clock), .Clr(Clear), .Q(out_7));  // open: nQ

  // Notes on the sheet:
  //   Registro de configuración
  //   0 -> input
  //   1 -> output
  //   Registro de control (Salida)
  //   Registro de almacenamiento (Entrada)
endmodule
